// Logisim project Circuito Saida 1.circ as structural Verilog: 1 circuit, main circuit main
module main (
  input  A,
  input  B,
  input  C
);

  wire A_prime_B_prime_C_out, A_prime_BC_prime_out, not_1_out, not_2_out, not_3_out, or_1_out;

  not not_1 (not_1_out, A);
  not not_2 (not_2_out, B);
  not not_3 (not_3_out, C);
  and A_prime_B_prime_C (A_prime_B_prime_C_out, not_1_out, not_2_out, C);
  and A_prime_BC_prime (A_prime_BC_prime_out, not_1_out, B, not_3_out);
  or or_1 (or_1_out, A_prime_B_prime_C_out, A_prime_BC_prime_out);
endmodule
