// Logisim project JOGADOR 2.circ as structural Verilog: 1 circuit, main circuit main
module main (
  input  in_1,
  input  in_2,
  input  in_3,
  input  in_4,
  input  in_5,
  input  in_6,
  input  in_7,
  input  in_8,
  input  in_9,
  input  in_10,
  input  in_11,
  input  in_12
);

  wire [1:0] and_1_out, and_2_out, and_3_out, or_1_out;
  wire [1:1] undriven, undriven_2, undriven_3, undriven_4, undriven_5, undriven_6, undriven_7, undriven_8,
       undriven_9, undriven_10, undriven_11, undriven_12;

  assign and_1_out = ~{undriven[1], in_1} & {undriven_2[1], in_2} & {undriven_3[1], in_3} & ~{undriven_11[1], in_4};  // AND_Gate and_1, 2 bits wide
  assign and_2_out = {undriven_4[1], in_5} & ~{undriven_5[1], in_6} & {undriven_6[1], in_7} & {undriven_10[1], in_8};  // AND_Gate and_2, 2 bits wide
  assign and_3_out = {undriven_7[1], in_9} & {undriven_8[1], in_10} & ~{undriven_9[1], in_11} & {undriven_12[1], in_12};  // AND_Gate and_3, 2 bits wide
  assign or_1_out = and_1_out | and_2_out | and_3_out;  // OR_Gate or_1, 2 bits wide
  // Pins of 1 and 2 bits meet at {undriven_5[1], in_6}
  // Pins of 1 and 2 bits meet at {undriven_2[1], in_2}
  // Pins of 1 and 2 bits meet at {undriven_6[1], in_7}
  // Pins of 1 and 2 bits meet at {undriven_9[1], in_11}
  // Pins of 1 and 2 bits meet at {undriven_7[1], in_9}
  // Pins of 1 and 2 bits meet at {undriven_8[1], in_10}
  // Pins of 1 and 2 bits meet at {undriven_12[1], in_12}
  // Pins of 1 and 2 bits meet at {undriven[1], in_1}
  // Pins of 1 and 2 bits meet at {undriven_11[1], in_4}
  // Pins of 1 and 2 bits meet at {undriven_10[1], in_8}
  // Pins of 1 and 2 bits meet at {undriven_3[1], in_3}
  // Pins of 1 and 2 bits meet at {undriven_4[1], in_5}

  // Notes on the sheet:
  //   A´BCD´+AB´CD+ABC´D
  //   JOGADOR 2
endmodule
