// Logisim project Loude Djema Trabalho Final.circ as structural Verilog: 2 circuits, main circuit Circuitos Seq. Op. ULA
// S
module Circuitos_Seq__Op__ULA (
  input  A,
  input  B
);

  wire [7:0] adder_1_out, and_1_out, divider_1_out, multiplier_1_out, nor_1_out, or_1_out, subtractor_1_out,
       xor_1_out;
  wire [7:1] undriven, undriven_2;

  assign or_1_out = {undriven, A} | {undriven_2, B};  // OR_Gate or_1, 8 bits wide
  assign and_1_out = {undriven, A} & {undriven_2, B};  // AND_Gate and_1, 8 bits wide
  assign xor_1_out = {undriven, A} ^ {undriven_2, B};  // XOR_Gate xor_1, 8 bits wide
  assign nor_1_out = ~({undriven, A} | {undriven_2, B});  // NOR_Gate nor_1, 8 bits wide
  Adder adder_1 (.a({undriven, A}), .b({undriven_2, B}), .out(adder_1_out));  // open: cin, cout
  Subtractor subtractor_1 (.a({undriven, A}), .b({undriven_2, B}), .out(subtractor_1_out));  // open: bin, bout
  Divider divider_1 (.a({undriven_2, B}), .b({undriven, A}), .out(divider_1_out));  // open: upper, rem
  Multiplier multiplier_1 (.a({undriven_2, B}), .b({undriven, A}), .out(multiplier_1_out));  // open: cin, cout
  Multiplexer #(.select(3), .width(8), .enable("false")) multiplexer_1 (
    .in0(or_1_out), .in1(and_1_out), .in2(xor_1_out), .in3(nor_1_out), .in4(adder_1_out),
    .in5(subtractor_1_out), .in6(divider_1_out), .in7(multiplier_1_out));  // open: out, sel
  // Pins of 1 and 8 bits meet at {undriven, A}
  // Pins of 1 and 8 bits meet at {undriven_2, B}
endmodule

module Ula (
  input  [7:0] A,
  input  [7:0] B,
  input  [2:0] in_3,
  input  C,
  input  in_5,
  output [7:0] Saida,
  output [7:0] out_7
);

  wire adder_1_cout, and_2_out, subtractor_1_bout;
  wire [7:0] adder_1_out, and_1_out, divider_1_out, multiplier_1_out, nor_1_out, or_1_out, subtractor_1_out,
       xor_1_out;

  assign or_1_out = A | B;  // OR_Gate or_1, 8 bits wide
  Subtractor subtractor_1 (.a(A), .b(B), .out(subtractor_1_out), .bin(C), .bout(subtractor_1_bout));
  assign and_1_out = A & B;  // AND_Gate and_1, 8 bits wide
  Adder adder_1 (.a(A), .b(B), .out(adder_1_out), .cin(C), .cout(adder_1_cout));
  Divider divider_1 (.a(A), .b(B), .out(divider_1_out), .rem(out_7));  // open: upper
  assign xor_1_out = A ^ B;  // XOR_Gate xor_1, 8 bits wide
  Multiplier multiplier_1 (.a(A), .b(B), .out(multiplier_1_out));  // open: cin, cout
  assign nor_1_out = ~(A | B);  // NOR_Gate nor_1, 8 bits wide
  Demultiplexer #(.enable("false")) demultiplexer_1 (
    .out0(subtractor_1_bout), .out1(adder_1_cout), .in(in_5), .sel(and_2_out));
  Multiplexer #(.select(3), .width(8), .enable("false")) multiplexer_1 (
    .in0(or_1_out), .in1(subtractor_1_out), .in2(and_1_out), .in3(adder_1_out), .in4(divider_1_out),
    .in5(xor_1_out), .in6(multiplier_1_out), .in7(nor_1_out), .out(Saida), .sel(in_3));
  and and_2 (and_2_out, in_3[2], in_3[1], ~in_3[0]);  // AND_Gate
endmodule
