// Logisim project trabalhofinalcircuitos.circ as structural Verilog: 11 circuits, main circuit main
module main (
  input  [7:0] Entrada,
  input  SEL,
  input  [1:0] RB,
  input  [1:0] RA,
  input  [1:0] RW,
  input  ESCREVE,
  input  [2:0] SEL_2,
  output [7:0] VW,
  output [7:0] out_9,
  output [7:0] out_10,
  output out_11,
  output out_12,
  output [7:0] RESTO_DO_DIV,
  output [7:0] out_14
);

  LED led_1 (.in(out_12));
  MUX_8 mux_8_1 (.Entrada_A(Entrada), .Sel_valor(SEL), .Entrada_B(out_14), .Saida(VW));
  Registrador registrador_1 (
    .Entrada(VW), .SEL_A(RA), .SEL_B(RB), .Escreve(ESCREVE), .Sel_RW(RW), .VB(out_10), .VA(out_9));
  ULA ula_1 (
    .A(out_9), .B(out_10), .Saida(out_14), .SEL(SEL_2), .Saida_C(out_11), .\Resto_Da_divisão (RESTO_DO_DIV),
    .out_5(out_12));
  LED led_2 (.in(out_11));
endmodule

module Registrador (
  input  [7:0] Entrada,
  input  Escreve,
  input  [1:0] Sel_RW,
  input  [1:0] SEL_A,
  input  [1:0] SEL_B,
  output [7:0] VA,
  output [7:0] VB
);

  wire demultiplexer_1_out0, demultiplexer_1_out1, demultiplexer_1_out2, demultiplexer_1_out3;
  wire [7:0] register_1_q, register_2_q, register_3_q, register_4_q;

  Register register_1 (.D(Entrada), .Q(register_1_q), .clk(demultiplexer_1_out3));  // open: en, clr
  Register register_2 (.D(Entrada), .Q(register_2_q), .clk(demultiplexer_1_out2));  // open: en, clr
  Register register_3 (.D(Entrada), .Q(register_3_q), .clk(demultiplexer_1_out1));  // open: en, clr
  Register register_4 (.D(Entrada), .Q(register_4_q), .clk(demultiplexer_1_out0));  // open: en, clr
  Demultiplexer #(.select(2), .enable("false")) demultiplexer_1 (
    .out0(demultiplexer_1_out0), .out1(demultiplexer_1_out1), .out2(demultiplexer_1_out2),
    .out3(demultiplexer_1_out3), .in(Escreve), .sel(Sel_RW));
  Multiplexer #(.select(2), .width(8), .enable("false")) multiplexer_1 (
    .in0(register_4_q), .in1(register_3_q), .in2(register_2_q), .in3(register_1_q), .out(VB), .sel(SEL_B));
  Multiplexer #(.select(2), .width(8), .enable("false")) multiplexer_2 (
    .in0(register_4_q), .in1(register_3_q), .in2(register_2_q), .in3(register_1_q), .out(VA), .sel(SEL_A));
endmodule

module ULA (
  input  [7:0] A,
  input  [7:0] B,
  input  [2:0] SEL,
  output [7:0] Saida,
  output out_5,
  output [7:0] \Resto_Da_divisão ,
  output Saida_C
);

  wire and_2_out;
  wire [7:0] add_8_1_out_4, addsu_1_saida, and_1_out, divider_1_out, multiplier_1_out, nor_1_out, or_1_out,
       xor_1_out, zero_1_out_4;

  AddSu addsu_1 (.Entrada_A(A), .Negado(and_2_out), .Entrada_B(B), .Carry_out(Saida_C), .Saida(addsu_1_saida));
  ADD_8 add_8_1 (.Entrada_A(A), .Entrada_B(B), .Carry_out(Saida_C), .out_4(add_8_1_out_4));
  assign or_1_out = A | B;  // OR_Gate or_1, 8 bits wide
  assign and_1_out = A & B;  // AND_Gate and_1, 8 bits wide
  Divider divider_1 (.a(A), .b(B), .out(divider_1_out), .rem(\Resto_Da_divisão ));  // open: upper
  assign xor_1_out = A ^ B;  // XOR_Gate xor_1, 8 bits wide
  Multiplier multiplier_1 (.a(A), .b(B), .out(multiplier_1_out));  // open: cin, cout
  assign nor_1_out = ~(A | B);  // NOR_Gate nor_1, 8 bits wide
  Multiplexer #(.select(3), .width(8), .enable("false")) multiplexer_1 (
    .in0(or_1_out), .in1(addsu_1_saida), .in2(and_1_out), .in3(add_8_1_out_4), .in4(divider_1_out),
    .in5(xor_1_out), .in6(multiplier_1_out), .in7(nor_1_out), .out(Saida), .sel(SEL));
  and and_2 (and_2_out, ~SEL[2], ~SEL[1], SEL[0]);  // AND_Gate
  Zero zero_1 (._0(SEL[0]), ._1(SEL[1]), ._2(SEL[2]), .out_4(zero_1_out_4));
  Comparator comparator_1 (.a(Saida), .b(zero_1_out_4), .eq(out_5));  // open: gt, lt
endmodule

module MUX_2x1 (
  input  Entrada_1,
  input  sel,
  input  Entrada_2,
  output Saida
);

  wire and_1_out, and_2_out, not_1_out;

  not not_1 (not_1_out, sel);
  and and_1 (and_1_out, Entrada_1, not_1_out);
  and and_2 (and_2_out, sel, Entrada_2);
  or or_1 (Saida, and_1_out, and_2_out);
endmodule

module MUX_8 (
  input  [7:0] Entrada_A,
  input  Sel_valor,
  input  [7:0] Entrada_B,
  output [7:0] Saida
);

  MUX_2x1 mux_2x1_1 (.Entrada_1(Entrada_A[3]), .sel(Sel_valor), .Entrada_2(Entrada_B[3]), .Saida(Saida[3]));
  MUX_2x1 mux_2x1_2 (.Entrada_1(Entrada_A[7]), .sel(Sel_valor), .Entrada_2(Entrada_B[7]), .Saida(Saida[7]));
  MUX_2x1 mux_2x1_3 (.Entrada_1(Entrada_A[2]), .sel(Sel_valor), .Entrada_2(Entrada_B[2]), .Saida(Saida[2]));
  MUX_2x1 mux_2x1_4 (.Entrada_1(Entrada_A[6]), .sel(Sel_valor), .Entrada_2(Entrada_B[6]), .Saida(Saida[6]));
  MUX_2x1 mux_2x1_5 (.Entrada_1(Entrada_A[1]), .sel(Sel_valor), .Entrada_2(Entrada_B[1]), .Saida(Saida[1]));
  MUX_2x1 mux_2x1_6 (.Entrada_1(Entrada_A[5]), .sel(Sel_valor), .Entrada_2(Entrada_B[5]), .Saida(Saida[5]));
  MUX_2x1 mux_2x1_7 (.Entrada_1(Entrada_A[0]), .sel(Sel_valor), .Entrada_2(Entrada_B[0]), .Saida(Saida[0]));
  MUX_2x1 mux_2x1_8 (.Entrada_1(Entrada_A[4]), .sel(Sel_valor), .Entrada_2(Entrada_B[4]), .Saida(Saida[4]));
endmodule

module Zero (
  input  _0,
  input  _1,
  input  _2,
  output [7:0] out_4
);

  wire and_1_out, and_2_out;

  and and_1 (and_1_out, _0, _1, _2);
  and and_2 (and_2_out, ~_0, _1, _2);  // AND_Gate
  and and_3 (out_4[7], and_1_out, and_2_out);

  assign out_4[6:0] = {7{out_4[7]}};
endmodule

module Add_1 (
  input  Entrada_A,
  input  Entrada_B,
  input  Carry_in,
  output Saida,
  output Carry_out
);

  wire and_1_out, and_2_out, and_3_out, xor_1_out;

  xor xor_1 (xor_1_out, Entrada_A, Entrada_B);
  and and_1 (and_1_out, Entrada_A, Entrada_B);
  and and_2 (and_2_out, Entrada_A, Carry_in);
  and and_3 (and_3_out, Entrada_B, Carry_in);
  xor xor_2 (Saida, xor_1_out, Carry_in);
  or or_1 (Carry_out, and_1_out, and_2_out, and_3_out);
endmodule

module ADD_8 (
  input  [7:0] Entrada_A,
  input  [7:0] Entrada_B,
  output Carry_out,
  output [7:0] out_4
);

  wire add_1_1_carry_out, add_1_3_carry_out, add_1_4_carry_out, add_1_5_carry_out, add_1_6_carry_out,
       add_1_7_carry_out, add_1_8_carry_out;

  Add_1 add_1_1 (
    .Entrada_A(Entrada_A[3]), .Entrada_B(Entrada_B[3]), .Carry_in(add_1_3_carry_out), .Saida(out_4[3]),
    .Carry_out(add_1_1_carry_out));
  Add_1 add_1_2 (
    .Entrada_A(Entrada_A[7]), .Entrada_B(Entrada_B[7]), .Carry_in(add_1_4_carry_out), .Saida(out_4[7]),
    .Carry_out(Carry_out));
  Add_1 add_1_3 (
    .Entrada_A(Entrada_A[2]), .Entrada_B(Entrada_B[2]), .Carry_in(add_1_5_carry_out), .Saida(out_4[2]),
    .Carry_out(add_1_3_carry_out));
  Add_1 add_1_4 (
    .Entrada_A(Entrada_A[6]), .Entrada_B(Entrada_B[6]), .Carry_in(add_1_6_carry_out), .Saida(out_4[6]),
    .Carry_out(add_1_4_carry_out));
  Add_1 add_1_5 (
    .Entrada_A(Entrada_A[1]), .Entrada_B(Entrada_B[1]), .Carry_in(add_1_7_carry_out), .Saida(out_4[1]),
    .Carry_out(add_1_5_carry_out));
  Add_1 add_1_6 (
    .Entrada_A(Entrada_A[5]), .Entrada_B(Entrada_B[5]), .Carry_in(add_1_8_carry_out), .Saida(out_4[5]),
    .Carry_out(add_1_6_carry_out));
  Add_1 add_1_7 (
    .Entrada_A(Entrada_A[0]), .Entrada_B(Entrada_B[0]), .Carry_in(1'b0), .Saida(out_4[0]),
    .Carry_out(add_1_7_carry_out));
  Add_1 add_1_8 (
    .Entrada_A(Entrada_A[4]), .Entrada_B(Entrada_B[4]), .Carry_in(add_1_1_carry_out), .Saida(out_4[4]),
    .Carry_out(add_1_8_carry_out));
endmodule

module Subs_1 (
  input  Negado,
  input  Entrada,
  output Saida
);

  wire not_1_out;

  MUX_2x1 mux_2x1_1 (.Entrada_1(Entrada), .sel(Negado), .Entrada_2(not_1_out), .Saida(Saida));
  not not_1 (not_1_out, Entrada);
endmodule

module Subs_8 (
  input  Negado,
  input  [7:0] Entrada,
  output [7:0] Saida
);

  Subs_1 subs_1_1 (.Entrada(Entrada[3]), .Negado(Negado), .Saida(Saida[3]));
  Subs_1 subs_1_2 (.Entrada(Entrada[7]), .Negado(Negado), .Saida(Saida[7]));
  Subs_1 subs_1_3 (.Entrada(Entrada[2]), .Negado(Negado), .Saida(Saida[2]));
  Subs_1 subs_1_4 (.Entrada(Entrada[6]), .Negado(Negado), .Saida(Saida[6]));
  Subs_1 subs_1_5 (.Entrada(Entrada[1]), .Negado(Negado), .Saida(Saida[1]));
  Subs_1 subs_1_6 (.Entrada(Entrada[5]), .Negado(Negado), .Saida(Saida[5]));
  Subs_1 subs_1_7 (.Entrada(Entrada[0]), .Negado(Negado), .Saida(Saida[0]));
  Subs_1 subs_1_8 (.Entrada(Entrada[4]), .Negado(Negado), .Saida(Saida[4]));
endmodule

module AddSu (
  input  Carry_out,
  input  [7:0] Entrada_A,
  input  Negado,
  input  [7:0] Entrada_B,
  output [7:0] Saida
);

  wire add_1_1_carry_out, add_1_3_carry_out, add_1_4_carry_out, add_1_5_carry_out, add_1_6_carry_out,
       add_1_7_carry_out, add_1_8_carry_out;
  wire [7:0] subs_8_1_saida;

  Subs_8 subs_8_1 (.Negado(Negado), .Entrada(Entrada_B), .Saida(subs_8_1_saida));
  Add_1 add_1_1 (
    .Entrada_A(Entrada_A[3]), .Entrada_B(subs_8_1_saida[3]), .Carry_in(add_1_3_carry_out), .Saida(Saida[3]),
    .Carry_out(add_1_1_carry_out));
  Add_1 add_1_2 (
    .Entrada_A(Entrada_A[7]), .Entrada_B(subs_8_1_saida[7]), .Carry_in(add_1_4_carry_out), .Saida(Saida[7]),
    .Carry_out(Carry_out));
  Add_1 add_1_3 (
    .Entrada_A(Entrada_A[2]), .Entrada_B(subs_8_1_saida[2]), .Carry_in(add_1_5_carry_out), .Saida(Saida[2]),
    .Carry_out(add_1_3_carry_out));
  Add_1 add_1_4 (
    .Entrada_A(Entrada_A[6]), .Entrada_B(subs_8_1_saida[6]), .Carry_in(add_1_6_carry_out), .Saida(Saida[6]),
    .Carry_out(add_1_4_carry_out));
  Add_1 add_1_5 (
    .Entrada_A(Entrada_A[1]), .Entrada_B(subs_8_1_saida[1]), .Carry_in(add_1_7_carry_out), .Saida(Saida[1]),
    .Carry_out(add_1_5_carry_out));
  Add_1 add_1_6 (
    .Entrada_A(Entrada_A[5]), .Entrada_B(subs_8_1_saida[5]), .Carry_in(add_1_8_carry_out), .Saida(Saida[5]),
    .Carry_out(add_1_6_carry_out));
  Add_1 add_1_7 (
    .Entrada_A(Entrada_A[0]), .Entrada_B(subs_8_1_saida[0]), .Carry_in(Negado), .Saida(Saida[0]),
    .Carry_out(add_1_7_carry_out));
  Add_1 add_1_8 (
    .Entrada_A(Entrada_A[4]), .Entrada_B(subs_8_1_saida[4]), .Carry_in(add_1_1_carry_out), .Saida(Saida[4]),
    .Carry_out(add_1_8_carry_out));
endmodule
